# Fritzing sketch wiring (saved by Fritzing 0.9.3b)
perfboards: 1

parts:
  Q1 = MOSFET-NCHANNEL [package=to220v]
  U1 = ATTINY13 [package=dip]
  S1 = Round Pushbutton
  U2 = LIPO-1000mAh [package=lipo-1000]
  MCU1 = Raspberry Pi Zero
  R1 = Resistor [tolerance=±5% resistance=220 package=THT]

nets:
  N1: Q1.G, U1.GND, U2.-, MCU1.pin_40
  N2: Q1.D, MCU1.pin_2, MCU1.pin_4
  N3: Q1.S, U1.PB0(MOSI)
  N4: U1.PB3(ADC3), R1.Pin_0
  N5: U1.PB4(ADC2), U2.+
  N6: U1.PB2(SCK_ADC1), MCU1.pin_22
  N7: U1.VCC, S1.leg1
  N8: MCU1.pin_37, R1.Pin_1
